// Logisim project CPU_AYAD_METIDJI.circ as structural Verilog: 34 circuits, main circuit CPU_V1
module CPU_V1 (
  output [3:0] out_1,
  output [3:0] out_2,
  output [3:0] out_3,
  output [11:0] out_4,
  output [2:0] out_5,
  output [3:0] \Adress_de_données 
);

  wire Clock_out, Reset_out, u_control_1_ext1, u_control_1_ext2, u_control_1_fetch, u_control_1_ra1,
       u_control_1_ra2, u_control_1_rb1, u_control_1_rb2, u_control_1_rc1, u_control_1_rc2, u_control_1_rd1,
       u_control_1_rd2, u_control_1_read, u_control_1_wa, u_control_1_wad, u_control_1_wb, u_control_1_wc,
       u_control_1_wd, u_control_1_wpc, u_control_1_write, ual_4bit_1_null, ual_4bit_1_overflow;
  wire [3:0] mux_2_4_1_out, ram_1_data, u_adressage_1_pcout, u_control_1_ad_out, u_control_1_pc_out;

  ROM #(.addrWidth(4), .dataWidth(12)) rom_1 (.addr(u_adressage_1_pcout), .data(out_4), .sel(1'b1));
  RAM #(.addrWidth(4), .dataWidth(4), .bus("separate")) ram_1 (
    .addr(\Adress_de_données ), .din(out_2), .data(ram_1_data), .str(u_control_1_write), .sel(1'b1),
    .clk(Clock_out), .ld(u_control_1_read), .clr(Reset_out));
  Clock Clock (.out(Clock_out));
  MUX_2_4 mux_2_4_1 (.OUT(mux_2_4_1_out), .in_0(ram_1_data), .in_1(out_2), .sel(u_control_1_read));
  Button Reset (.out(Reset_out));
  U_adressage u_adressage_1 (
    .WriteAd(u_control_1_wad), .WritePc(u_control_1_wpc), .RESET(Reset_out), .PcIn(u_control_1_pc_out),
    .AdIn(u_control_1_ad_out), .Clock(Clock_out), .READ(1'b1), .AdOut(\Adress_de_données ),
    .PcOut(u_adressage_1_pcout));
  Banc_4_registres banc_4_registres_1 (
    .Data_IN(mux_2_4_1_out), .WA(u_control_1_wa), .WB(u_control_1_wb), .WC(u_control_1_wc),
    .WD(u_control_1_wd), .CLK(Clock_out), .RESET(Reset_out), .rA1(u_control_1_ra2), .rB1(u_control_1_rb2),
    .rC1(u_control_1_rc2), .rD1(u_control_1_rd2), .rA2(u_control_1_ra1), .rB2(u_control_1_rb1),
    .rC2(u_control_1_rc1), .rD2(u_control_1_rd1), .OUT_x(out_1), .OUT_y(out_3));
  U_control u_control_1 (
    .instruction(out_4), .wAD(u_control_1_wad), .AD_out(u_control_1_ad_out), .wPC(u_control_1_wpc),
    .Fetch(u_control_1_fetch), .PC_out(u_control_1_pc_out), .wA(u_control_1_wa), .wB(u_control_1_wb),
    .wC(u_control_1_wc), .wD(u_control_1_wd), .rA1(u_control_1_ra1), .rA2(u_control_1_ra2),
    .rB1(u_control_1_rb1), .rB2(u_control_1_rb2), .rC1(u_control_1_rc1), .rC2(u_control_1_rc2),
    .rD1(u_control_1_rd1), .rD2(u_control_1_rd2), .f0(out_5[0]), .f1(out_5[1]), .f2(out_5[2]),
    .CLK(Clock_out), .reset(Reset_out), .ext1(u_control_1_ext1), .ext2(u_control_1_ext2),
    .write(u_control_1_write), .read(u_control_1_read), .PC_in(u_adressage_1_pcout));
  LED Fetch (.in(u_control_1_fetch));
  UAL_4bit ual_4bit_1 (
    .nombre_1(out_1), .operation(out_5), .nombre_2(out_3), .Resultat(out_2), .OverFlow(ual_4bit_1_overflow),
    .NULL(ual_4bit_1_null), .En1(u_control_1_ext1), .En2(u_control_1_ext2));
  LED OverFlow (.in(ual_4bit_1_overflow));
  Hex_Digit_Display hex_digit_display_1 (.value(out_2));  // open: dp
  LED Null (.in(ual_4bit_1_null));

  // Notes on the sheet:
  //   contents of rom_1 (hex, n*v repeats v):
  //   400 444 384 4c8 148 234 80c c73 662 12 66 247 745 235 12 cab
endmodule

module MUX_1_2 (
  input  e0,
  input  e1,
  input  Sel,
  output out_4
);

  wire AND2_2_out, AND2_out, not_1_out;

  not not_1 (not_1_out, Sel);
  and AND2 (AND2_out, e0, not_1_out);
  and AND2_2 (AND2_2_out, e1, Sel);
  or OR2 (out_4, AND2_out, AND2_2_out);

  // Notes on the sheet:
  //   e0
  //   e1
endmodule

module MUX_1_8 (
  input  D0,
  input  D1,
  input  D2,
  input  D3,
  input  D4,
  input  D5,
  input  D6,
  input  D7,
  input  A,
  input  B,
  input  C,
  output S
);

  wire AND4_2_out, AND4_3_out, AND4_4_out, AND4_5_out, AND4_6_out, AND4_7_out, AND4_8_out, AND4_out,
       not_1_out, not_2_out, not_3_out;

  not not_1 (not_1_out, A);
  not not_2 (not_2_out, B);
  not not_3 (not_3_out, C);
  and AND4 (AND4_out, D0, not_1_out, not_2_out, not_3_out);
  and AND4_2 (AND4_2_out, D1, not_1_out, not_2_out, C);
  and AND4_3 (AND4_3_out, D2, not_1_out, B, not_3_out);
  and AND4_4 (AND4_4_out, D3, not_1_out, B, C);
  and AND4_5 (AND4_5_out, D4, A, not_2_out, not_3_out);
  and AND4_6 (AND4_6_out, D5, A, not_2_out, C);
  and AND4_7 (AND4_7_out, D6, A, B, not_3_out);
  and AND4_8 (AND4_8_out, D7, A, A, C);
  or OR8 (S, AND4_out, AND4_2_out, AND4_3_out, AND4_4_out, AND4_5_out, AND4_6_out, AND4_7_out, AND4_8_out);

  // Notes on the sheet:
  //   ┬
  //   A
  //   ┬
  //   B
  //   C
  //   ┬
endmodule

// Decoder
module Decoder_3_8 (
  input  e0,
  input  e1,
  input  e2,
  output D0,
  output D1,
  output D2,
  output D3,
  output D4,
  output D5,
  output D6,
  output D7
);

  wire not_1_out, not_2_out, not_3_out;

  not not_1 (not_1_out, e0);
  not not_2 (not_2_out, e1);
  not not_3 (not_3_out, e2);
  and AND3 (D0, not_1_out, not_2_out, not_3_out);
  and AND3_2 (D1, not_1_out, not_2_out, e2);
  and AND3_3 (D2, not_1_out, e1, not_3_out);
  and AND3_4 (D3, not_1_out, e1, e2);
  and AND3_5 (D4, e0, not_2_out, not_3_out);
  and AND3_6 (D5, e0, not_2_out, e2);
  and AND3_7 (D6, e0, e1, not_3_out);
  and AND3_8 (D7, e0, e1, e2);

  // Notes on the sheet:
  //   ┬
  //   e0
  //   ┬
  //   e2
  //   e1
  //   ┬
endmodule

// Decoder
module Decoder_2_4 (
  input  [1:0] E,
  output D0,
  output D1,
  output D2,
  output D3
);

  wire not_1_out, not_2_out;

  not not_1 (not_1_out, E[1]);
  not not_2 (not_2_out, E[0]);
  and AND2 (D0, not_1_out, not_2_out);
  and AND2_2 (D1, not_1_out, E[0]);
  and AND2_3 (D2, E[1], not_2_out);
  and AND2_4 (D3, E[1], E[0]);

  // Notes on the sheet:
  //   e0
  //   ┬
  //   ┬
  //   e1
endmodule

module comparateur_4 (
  input  [3:0] A,
  input  [3:0] B,
  output A_B
);

  wire XOR2_2_out, XOR2_3_out, XOR2_4_out, XOR2_out;

  xor XOR2 (XOR2_out, A[3], B[3]);
  xor XOR2_2 (XOR2_2_out, A[2], B[2]);
  xor XOR2_3 (XOR2_3_out, A[1], B[1]);
  xor XOR2_4 (XOR2_4_out, A[0], B[0]);
  nor nor_1 (A_B, XOR2_out, XOR2_2_out, XOR2_3_out, XOR2_4_out);
endmodule

module PLA_majoritaire (
  input  A,
  input  B,
  input  C,
  output S
);

  wire AND3_2_out, AND3_3_out, AND3_4_out, AND3_out, not_1_out, not_2_out, not_3_out;

  not not_1 (not_1_out, A);
  not not_2 (not_2_out, B);
  not not_3 (not_3_out, C);
  and AND3 (AND3_out, not_1_out, B, C);
  and AND3_2 (AND3_2_out, A, not_2_out, C);
  and AND3_3 (AND3_3_out, A, B, not_3_out);
  and AND3_4 (AND3_4_out, A, B, C);
  or OR4 (S, AND3_out, AND3_2_out, AND3_3_out, AND3_4_out);

  // Notes on the sheet:
  //   ┬
  //   ┬
  //   A
  //   B
  //   ┬
  //   C
endmodule

module \Machine_Café_bouillon  (
  input  sucre,
  input  sel,
  input  \Café ,
  input  Boullion
);

  wire AND2_2_out, AND2_3_out, AND2_out, not_1_out, not_2_out, OR3_out;

  not not_1 (not_1_out, \Café );
  not not_2 (not_2_out, Boullion);
  and AND2 (AND2_out, \Café , Boullion);
  and AND2_2 (AND2_2_out, sucre, not_1_out);
  and AND2_3 (AND2_3_out, not_2_out, sel);
  or OR3 (OR3_out, AND2_out, AND2_2_out, AND2_3_out);
  LED Voyant (.in(OR3_out));

  // Notes on the sheet:
  //   Sucre
  //   ┬
  //   Sel
  //   C
  //   ┬
  //   B
endmodule

module Half_adder (
  input  A,
  input  B,
  output Somme,
  output Retenue
);

  and AND2 (Retenue, A, B);
  xor XOR2 (Somme, A, B);
endmodule

// +
module Full_adder (
  input  Re,
  input  A,
  input  B,
  output S,
  output Rs
);

  wire AND2_2_out, AND2_out, XOR2_out;

  and AND2 (AND2_out, A, B);
  xor XOR2 (XOR2_out, A, B);
  or OR2 (Rs, AND2_out, AND2_2_out);
  and AND2_2 (AND2_2_out, XOR2_out, Re);
  xor XOR2_2 (S, Re, XOR2_out);
endmodule

module Full_adder_4bit (
  input  [3:0] number_1,
  input  [3:0] number_2,
  output [3:0] Somme,
  output OverFlow
);

  wire Full_adder_2_rs, Full_adder_rs, Half_adder_retenue;

  Half_adder Half_adder (.A(number_1[0]), .B(number_2[0]), .Retenue(Half_adder_retenue), .Somme(Somme[0]));
  Full_adder Full_adder (.A(number_1[1]), .B(number_2[1]), .Re(Half_adder_retenue), .Rs(Full_adder_rs), .S(Somme[1]));
  Full_adder Full_adder_2 (.A(number_1[2]), .B(number_2[2]), .Re(Full_adder_rs), .Rs(Full_adder_2_rs), .S(Somme[2]));
  Full_adder Full_adder_3 (.A(number_1[3]), .B(number_2[3]), .Re(Full_adder_2_rs), .Rs(OverFlow), .S(Somme[3]));
endmodule

module UAL (
  input  Cin,
  input  entrer_1,
  input  En1,
  input  entrer_2,
  input  En2,
  input  [2:0] F_s,
  output S,
  output Cout,
  output [2:0] Dec_Out
);

  wire AND2_2_out, AND2_3_out, AND2_4_out, AND2_5_out, AND2_6_out, AND2_7_out, AND2_8_out, AND2_9_out,
       AND2_10_out, AND2_11_out, AND2_12_out, AND2_13_out, AND2_out, decoder_3_8_1_d0, decoder_3_8_1_d1,
       decoder_3_8_1_d2, decoder_3_8_1_d3, decoder_3_8_1_d4, decoder_3_8_1_d5, decoder_3_8_1_d6,
       decoder_3_8_1_d7, full_adder_1_rs, full_adder_1_s, full_subtractor_1_borrow, full_subtractor_1_diff,
       not_1_out, NOTAND2_out, NOTOR2_out, NXOR2_out, OR2_out;

  and AND2 (AND2_out, entrer_1, En1);
  and AND2_2 (AND2_2_out, entrer_2, En2);
  not not_1 (not_1_out, AND2_2_out);
  and AND2_3 (AND2_3_out, AND2_out, AND2_2_out);
  or OR2 (OR2_out, AND2_2_out, AND2_out);
  Decoder_3_8 decoder_3_8_1 (
    .e0(F_s[2]), .e1(F_s[1]), .e2(F_s[0]), .D0(decoder_3_8_1_d0), .D1(decoder_3_8_1_d1),
    .D2(decoder_3_8_1_d2), .D3(decoder_3_8_1_d3), .D4(decoder_3_8_1_d4), .D5(decoder_3_8_1_d5),
    .D6(decoder_3_8_1_d6), .D7(decoder_3_8_1_d7));
  nor NOTOR2 (NOTOR2_out, AND2_out, AND2_2_out);
  nand NOTAND2 (NOTAND2_out, AND2_out, AND2_2_out);
  xnor NXOR2 (NXOR2_out, AND2_out, AND2_2_out);
  and AND2_4 (AND2_4_out, AND2_3_out, decoder_3_8_1_d2);
  and AND2_5 (AND2_5_out, not_1_out, decoder_3_8_1_d3);
  and AND2_6 (AND2_6_out, OR2_out, decoder_3_8_1_d1);
  and AND2_7 (AND2_7_out, full_adder_1_rs, decoder_3_8_1_d0);
  and AND2_8 (AND2_8_out, full_subtractor_1_borrow, decoder_3_8_1_d4);
  and AND2_9 (AND2_9_out, decoder_3_8_1_d0, full_adder_1_s);
  Full_adder full_adder_1 (.A(AND2_out), .B(AND2_2_out), .Re(Cin), .Rs(full_adder_1_rs), .S(full_adder_1_s));
  and AND2_10 (AND2_10_out, NOTOR2_out, decoder_3_8_1_d5);
  and AND2_11 (AND2_11_out, decoder_3_8_1_d4, full_subtractor_1_diff);
  Full_subtractor full_subtractor_1 (
    .A(AND2_out), .B(AND2_2_out), .C(Cin), .DIFF(full_subtractor_1_diff), .BORROW(full_subtractor_1_borrow));
  and AND2_12 (AND2_12_out, NOTAND2_out, decoder_3_8_1_d6);
  and AND2_13 (AND2_13_out, NXOR2_out, decoder_3_8_1_d7);
  or OR2_2 (Cout, AND2_7_out, AND2_8_out);
  or OR8 (S, AND2_4_out, AND2_5_out, AND2_6_out, AND2_9_out, AND2_10_out, AND2_11_out, AND2_12_out, AND2_13_out);

  assign Dec_Out = F_s;

  // Notes on the sheet:
  //   ┬
  //   B
  //   A
endmodule

module UAL_4bit (
  input  [3:0] nombre_1,
  input  [2:0] operation,
  input  En1,
  input  En2,
  input  [3:0] nombre_2,
  output OverFlow,
  output [3:0] Resultat,
  output NULL
);

  wire ual_1_cout, ual_2_cout, ual_3_cout;
  wire [2:0] ual_1_dec_out, ual_2_dec_out, ual_3_dec_out;

  UAL ual_1 (
    .entrer_1(nombre_1[0]), .entrer_2(nombre_2[0]), .F_s(operation), .S(Resultat[0]), .Cout(ual_1_cout),
    .Dec_Out(ual_1_dec_out), .Cin(1'b0), .En2(En2), .En1(En1));
  UAL ual_2 (
    .entrer_1(nombre_1[1]), .entrer_2(nombre_2[1]), .F_s(ual_1_dec_out), .S(Resultat[1]), .Cout(ual_2_cout),
    .Dec_Out(ual_2_dec_out), .Cin(ual_1_cout), .En2(En2), .En1(En1));
  UAL ual_3 (
    .entrer_1(nombre_1[2]), .entrer_2(nombre_2[2]), .F_s(ual_2_dec_out), .S(Resultat[2]), .Cout(ual_3_cout),
    .Dec_Out(ual_3_dec_out), .Cin(ual_2_cout), .En2(En2), .En1(En1));
  UAL ual_4 (
    .entrer_1(nombre_1[3]), .entrer_2(nombre_2[3]), .F_s(ual_3_dec_out), .S(Resultat[3]), .Cout(OverFlow),
    .Cin(ual_3_cout), .En2(En2), .En1(En1));  // open: Dec_Out
  comparateur_4 comparateur_4_1 (.A(Resultat), .B(4'b0000), .A_B(NULL));
endmodule

module Half_subtractor (
  input  enter_1,
  input  enter_2,
  output Substract,
  output retenue
);

  wire not_1_out;

  not not_1 (not_1_out, enter_1);
  xor XOR2 (Substract, enter_1, enter_2);
  and AND2 (retenue, not_1_out, enter_2);

  // Notes on the sheet:
  //   A
  //   ┬
  //   B
  //   A - B
endmodule

// -
module Full_subtractor (
  input  A,
  input  B,
  input  C,
  output DIFF,
  output BORROW
);

  wire AND2_2_out, AND2_3_out, AND2_out, not_1_out, XOR2_out;

  not not_1 (not_1_out, A);
  xor XOR2 (XOR2_out, A, B);
  and AND2 (AND2_out, not_1_out, B);
  and AND2_2 (AND2_2_out, B, C);
  and AND2_3 (AND2_3_out, not_1_out, C);
  xor XOR2_2 (DIFF, XOR2_out, C);
  or OR3 (BORROW, AND2_out, AND2_2_out, AND2_3_out);
endmodule

module Full_substractor_4bit (
  input  [3:0] number_1,
  input  [3:0] number_2,
  output [3:0] difference,
  output OverFlow
);

  wire Full_subtractor_2_borrow, Full_subtractor_3_borrow, Full_subtractor_borrow;

  Full_subtractor Full_subtractor (
    .A(number_1[0]), .B(number_2[0]), .C(1'b0), .DIFF(difference[0]), .BORROW(Full_subtractor_borrow));
  Full_subtractor Full_subtractor_2 (
    .A(number_1[1]), .B(number_2[1]), .C(Full_subtractor_borrow), .DIFF(difference[1]),
    .BORROW(Full_subtractor_2_borrow));
  Full_subtractor Full_subtractor_3 (
    .A(number_1[2]), .B(number_2[2]), .C(Full_subtractor_2_borrow), .DIFF(difference[2]),
    .BORROW(Full_subtractor_3_borrow));
  Full_subtractor Full_subtractor_4 (
    .A(number_1[3]), .B(number_2[3]), .C(Full_subtractor_3_borrow), .DIFF(difference[3]), .BORROW(OverFlow));
endmodule

module Verrou_RS (
  input  R,
  input  S,
  output Q,
  output Q_2
);

  nor nor_1 (Q, R, Q_2);
  nor nor_2 (Q_2, Q, S);
endmodule

module Bascule_RSH (
  input  Reset,
  input  Clock,
  input  Set,
  output Q,
  output Q_2
);

  wire AND2_2_out, AND2_out;

  and AND2 (AND2_out, Reset, Clock);
  and AND2_2 (AND2_2_out, Clock, Set);
  nor NOR2 (Q, AND2_out, Q_2);
  nor NOR2_2 (Q_2, Q, AND2_2_out);
endmodule

module Bascule_D (
  input  D,
  input  CLK,
  output Q,
  output Q_2
);

  wire AND2_2_out, AND2_out, not_1_out;

  not not_1 (not_1_out, D);
  and AND2 (AND2_out, not_1_out, CLK);
  and AND2_2 (AND2_2_out, CLK, D);
  nor NOR2 (Q, AND2_out, Q_2);
  nor NOR2_2 (Q_2, Q, AND2_2_out);

  // Notes on the sheet:
  //   R
  //   S
endmodule

module Bascule_JK (
  input  CLK,
  input  J,
  input  K,
  output Q,
  output Q_2
);

  wire AND2_2_out, AND2_out, not_1_out, or_1_out;

  not not_1 (not_1_out, K);
  and AND2 (AND2_out, Q_2, J);
  and AND2_2 (AND2_2_out, not_1_out, Q);
  or or_1 (or_1_out, AND2_out, AND2_2_out);
  D_Flip_Flop d_ff_1 (.clk(CLK), .D(or_1_out), .Q(Q), .Qn(Q_2));  // open: preset, en, reset
endmodule

module Bascule_T (
  input  CLK,
  input  T,
  output Q,
  output Q_2
);

  wire XOR2_out;

  xor XOR2 (XOR2_out, Q, T);
  D_Flip_Flop d_ff_1 (.clk(CLK), .D(XOR2_out), .Q(Q), .Qn(Q_2));  // open: preset, en, reset
endmodule

module Registre_4bit (
  input  [3:0] Data_in,
  input  Write,
  input  CLK,
  input  read1,
  input  read2,
  input  reset,
  output [3:0] Out_1,
  output [3:0] Out_2
);

  wire controlled_buffer_1_out, controlled_buffer_2_out, controlled_buffer_3_out, controlled_buffer_4_out,
       d_ff_1_q, d_ff_2_q, d_ff_3_q, d_ff_4_q;

  assign controlled_buffer_1_out = Write ? Data_in[1] : 1'bz;  // Controlled_Buffer controlled_buffer_1
  assign controlled_buffer_2_out = Write ? Data_in[2] : 1'bz;  // Controlled_Buffer controlled_buffer_2
  assign controlled_buffer_3_out = Write ? Data_in[3] : 1'bz;  // Controlled_Buffer controlled_buffer_3
  assign controlled_buffer_4_out = Write ? Data_in[0] : 1'bz;  // Controlled_Buffer controlled_buffer_4
  D_Flip_Flop d_ff_1 (.clk(CLK), .D(controlled_buffer_4_out), .Q(d_ff_1_q), .reset(reset));  // open: Qn, preset, en
  D_Flip_Flop d_ff_2 (.clk(CLK), .D(controlled_buffer_1_out), .Q(d_ff_2_q), .reset(reset));  // open: Qn, preset, en
  D_Flip_Flop d_ff_3 (.clk(CLK), .D(controlled_buffer_2_out), .Q(d_ff_3_q), .reset(reset));  // open: Qn, preset, en
  D_Flip_Flop d_ff_4 (.clk(CLK), .D(controlled_buffer_3_out), .Q(d_ff_4_q), .reset(reset));  // open: Qn, preset, en
  assign Out_2[0] = read2 ? d_ff_1_q : 1'bz;  // Controlled_Buffer controlled_buffer_5
  assign Out_2[1] = read2 ? d_ff_2_q : 1'bz;  // Controlled_Buffer controlled_buffer_6
  assign Out_2[2] = read2 ? d_ff_3_q : 1'bz;  // Controlled_Buffer controlled_buffer_7
  assign Out_1[0] = read1 ? d_ff_1_q : 1'bz;  // Controlled_Buffer controlled_buffer_8
  assign Out_1[1] = read1 ? d_ff_2_q : 1'bz;  // Controlled_Buffer controlled_buffer_9
  assign Out_2[3] = read2 ? d_ff_4_q : 1'bz;  // Controlled_Buffer controlled_buffer_10
  assign Out_1[2] = read1 ? d_ff_3_q : 1'bz;  // Controlled_Buffer controlled_buffer_11
  assign Out_1[3] = read1 ? d_ff_4_q : 1'bz;  // Controlled_Buffer controlled_buffer_12
endmodule

module Banc_4_registres (
  input  RESET,
  input  CLK,
  input  [3:0] Data_IN,
  input  WA,
  input  WB,
  input  WC,
  input  WD,
  input  rA2,
  input  rB2,
  input  rC2,
  input  rD2,
  input  rA1,
  input  rB1,
  input  rC1,
  input  rD1,
  output [3:0] OUT_x,
  output [3:0] OUT_y
);

  wire [3:0] registre_4bit_1_out_1, registre_4bit_1_out_2;

  Registre_4bit registre_4bit_1 (
    .Out_1(registre_4bit_1_out_1), .Data_in(Data_IN), .Out_2(registre_4bit_1_out_2), .Write(WA), .CLK(CLK),
    .read1(rA1), .read2(rA2), .reset(RESET));
  Registre_4bit registre_4bit_2 (
    .Out_1(registre_4bit_1_out_1), .Data_in(Data_IN), .Out_2(registre_4bit_1_out_2), .Write(WB), .CLK(CLK),
    .read1(rB1), .read2(rB2), .reset(RESET));
  Registre_4bit registre_4bit_3 (
    .Out_1(registre_4bit_1_out_1), .Data_in(Data_IN), .Out_2(registre_4bit_1_out_2), .Write(WC), .CLK(CLK),
    .read1(rC1), .read2(rC2), .reset(RESET));
  Registre_4bit registre_4bit_4 (
    .Out_1(registre_4bit_1_out_1), .Data_in(Data_IN), .Out_2(registre_4bit_1_out_2), .Write(WD), .CLK(CLK),
    .read1(rD1), .read2(rD2), .reset(RESET));
  Pull_Resistor pull_resistor_1 (.node(registre_4bit_1_out_2));
  assign OUT_x = registre_4bit_1_out_2 | registre_4bit_1_out_2 | registre_4bit_1_out_2 | registre_4bit_1_out_2;  // OR_Gate or_1, 4 bits wide
  Pull_Resistor pull_resistor_2 (.node(registre_4bit_1_out_1));
  assign OUT_y = registre_4bit_1_out_1 | registre_4bit_1_out_1 | registre_4bit_1_out_1 | registre_4bit_1_out_1;  // OR_Gate or_2, 4 bits wide
endmodule

module Compteur_7 (
  output Q2,
  output Q1,
  output Q0
);

  wire AND2_out, clock_1_out;

  Clock clock_1 (.out(clock_1_out));
  and AND2 (AND2_out, Q0, Q1);
  T_Flip_Flop t_ff_1 (.clk(clock_1_out), .T(AND2_out), .Q(Q2));  // open: Qn, preset, reset, en
  LED led_1 (.in(Q2));
  T_Flip_Flop t_ff_2 (.clk(clock_1_out), .T(Q0), .Q(Q1));  // open: Qn, preset, reset, en
  LED led_2 (.in(Q1));
  Hex_Digit_Display hex_digit_display_1 (.value({1'b0, Q2, Q1, Q0}));  // open: dp
  T_Flip_Flop t_ff_3 (.clk(clock_1_out), .T(1'b1), .Q(Q0));  // open: Qn, preset, reset, en
  LED led_3 (.in(Q0));
endmodule

module U_adressage (
  input  RESET,
  input  Clock,
  input  READ,
  input  [3:0] PcIn,
  input  [3:0] AdIn,
  input  WriteAd,
  input  WritePc,
  output [3:0] PcOut,
  output [3:0] AdOut
);

  Registre_AD registre_ad_1 (.Write_AD(WriteAd), .CLK(Clock), .Reset(RESET), .READ(READ), .In(AdIn), .Out(AdOut));
  Registre_PC registre_pc_1 (.Write_PC(WritePc), .CLK(Clock), .Reset(RESET), .READ(READ), .In(PcIn), .Out(PcOut));
endmodule

module Registre_PC (
  input  [3:0] In,
  input  Write_PC,
  input  CLK,
  input  Reset,
  input  READ,
  output [3:0] Out
);

  wire controlled_buffer_1_out, controlled_buffer_2_out, controlled_buffer_3_out, controlled_buffer_4_out,
       d_ff_1_q, d_ff_2_q, d_ff_3_q, d_ff_4_q;

  assign controlled_buffer_1_out = Write_PC ? In[3] : 1'bz;  // Controlled_Buffer controlled_buffer_1
  assign controlled_buffer_2_out = Write_PC ? In[2] : 1'bz;  // Controlled_Buffer controlled_buffer_2
  D_Flip_Flop d_ff_1 (.clk(CLK), .D(controlled_buffer_1_out), .Q(d_ff_1_q), .reset(Reset));  // open: Qn, preset, en
  and AND2 (Out[3], READ, d_ff_1_q);
  assign controlled_buffer_3_out = Write_PC ? In[1] : 1'bz;  // Controlled_Buffer controlled_buffer_3
  D_Flip_Flop d_ff_2 (.clk(CLK), .D(controlled_buffer_2_out), .Q(d_ff_2_q), .reset(Reset));  // open: Qn, preset, en
  and AND2_2 (Out[2], READ, d_ff_2_q);
  assign controlled_buffer_4_out = Write_PC ? In[0] : 1'bz;  // Controlled_Buffer controlled_buffer_4
  D_Flip_Flop d_ff_3 (.clk(CLK), .D(controlled_buffer_3_out), .Q(d_ff_3_q), .reset(Reset));  // open: Qn, preset, en
  and AND2_3 (Out[1], READ, d_ff_3_q);
  D_Flip_Flop d_ff_4 (.clk(CLK), .D(controlled_buffer_4_out), .Q(d_ff_4_q), .reset(Reset));  // open: Qn, preset, en
  and AND2_4 (Out[0], READ, d_ff_4_q);
endmodule

module Registre_AD (
  input  [3:0] In,
  input  Write_AD,
  input  CLK,
  input  Reset,
  input  READ,
  output [3:0] Out
);

  wire controlled_buffer_1_out, controlled_buffer_2_out, controlled_buffer_3_out, controlled_buffer_4_out,
       d_ff_1_q, d_ff_2_q, d_ff_3_q, d_ff_4_q;

  assign controlled_buffer_1_out = Write_AD ? In[3] : 1'bz;  // Controlled_Buffer controlled_buffer_1
  assign controlled_buffer_2_out = Write_AD ? In[2] : 1'bz;  // Controlled_Buffer controlled_buffer_2
  D_Flip_Flop d_ff_1 (.clk(CLK), .D(controlled_buffer_1_out), .Q(d_ff_1_q), .reset(Reset));  // open: Qn, preset, en
  and AND2 (Out[3], READ, d_ff_1_q);
  assign controlled_buffer_3_out = Write_AD ? In[1] : 1'bz;  // Controlled_Buffer controlled_buffer_3
  D_Flip_Flop d_ff_2 (.clk(CLK), .D(controlled_buffer_2_out), .Q(d_ff_2_q), .reset(Reset));  // open: Qn, preset, en
  and AND2_2 (Out[2], READ, d_ff_2_q);
  assign controlled_buffer_4_out = Write_AD ? In[0] : 1'bz;  // Controlled_Buffer controlled_buffer_4
  D_Flip_Flop d_ff_3 (.clk(CLK), .D(controlled_buffer_3_out), .Q(d_ff_3_q), .reset(Reset));  // open: Qn, preset, en
  and AND2_3 (Out[1], READ, d_ff_3_q);
  D_Flip_Flop d_ff_4 (.clk(CLK), .D(controlled_buffer_4_out), .Q(d_ff_4_q), .reset(Reset));  // open: Qn, preset, en
  and AND2_4 (Out[0], READ, d_ff_4_q);
endmodule

module Mux_1_4 (
  input  e0,
  input  e1,
  input  e2,
  input  e3,
  input  [1:0] sel,
  output S
);

  wire AND3_2_out, AND3_3_out, AND3_4_out, AND3_out, not_1_out, not_2_out;

  not not_1 (not_1_out, sel[1]);
  not not_2 (not_2_out, sel[0]);
  and AND3 (AND3_out, e0, not_1_out, not_2_out);
  and AND3_2 (AND3_2_out, e1, not_1_out, sel[0]);
  and AND3_3 (AND3_3_out, e2, sel[1], not_2_out);
  and AND3_4 (AND3_4_out, e3, sel[0], sel[1]);
  or OR4 (S, AND3_out, AND3_2_out, AND3_3_out, AND3_4_out);
endmodule

module MUX_4_4 (
  input  [3:0] in0,
  input  [3:0] in1,
  input  [3:0] in2,
  input  [3:0] in3,
  input  [1:0] sel,
  output [3:0] OUT
);

  Mux_1_4 mux_1_4_1 (.e0(in0[0]), .e1(in1[0]), .e2(in2[0]), .e3(in3[0]), .S(OUT[0]), .sel(sel));
  Mux_1_4 mux_1_4_2 (.e0(in0[1]), .e1(in1[1]), .e2(in2[1]), .e3(in3[1]), .S(OUT[1]), .sel(sel));
  Mux_1_4 mux_1_4_3 (.e0(in0[2]), .e1(in1[2]), .e2(in2[2]), .e3(in3[2]), .S(OUT[2]), .sel(sel));
  Mux_1_4 mux_1_4_4 (.e0(in0[3]), .e1(in1[3]), .e2(in2[3]), .e3(in3[3]), .S(OUT[3]), .sel(sel));
endmodule

module MUX_1_4bits (
  input  [3:0] in_0,
  input  [3:0] in_1,
  input  sel,
  output [3:0] OUT
);

  MUX_1_2 mux_1_2_1 (.e0(in_1[0]), .e1(sel), .Sel(in_0[0]), .out_4(OUT[0]));
  MUX_1_2 mux_1_2_2 (.e0(in_1[1]), .e1(sel), .Sel(in_0[1]), .out_4(OUT[1]));
  MUX_1_2 mux_1_2_3 (.e0(in_1[2]), .e1(sel), .Sel(in_0[2]), .out_4(OUT[2]));
  MUX_1_2 mux_1_2_4 (.e0(in_1[3]), .e1(sel), .Sel(in_0[3]), .out_4(OUT[3]));
endmodule

// REG12
module Registre_12bit (
  input  [11:0] In,
  input  write,
  input  rA1,
  input  rA2,
  input  CLK,
  input  Reset,
  output [11:0] outX,
  output [11:0] outY
);

  wire controlled_buffer_1_out, controlled_buffer_2_out, controlled_buffer_3_out, controlled_buffer_4_out,
       controlled_buffer_5_out, controlled_buffer_6_out, controlled_buffer_7_out, controlled_buffer_8_out,
       controlled_buffer_9_out, controlled_buffer_10_out, controlled_buffer_11_out, controlled_buffer_12_out,
       d_ff_1_q, d_ff_2_q, d_ff_3_q, d_ff_4_q, d_ff_5_q, d_ff_6_q, d_ff_7_q, d_ff_8_q, d_ff_9_q, d_ff_10_q,
       d_ff_11_q, d_ff_12_q;

  assign controlled_buffer_1_out = write ? In[0] : 1'bz;  // Controlled_Buffer controlled_buffer_1
  assign controlled_buffer_2_out = write ? In[1] : 1'bz;  // Controlled_Buffer controlled_buffer_2
  assign controlled_buffer_3_out = write ? In[2] : 1'bz;  // Controlled_Buffer controlled_buffer_3
  assign controlled_buffer_4_out = write ? In[3] : 1'bz;  // Controlled_Buffer controlled_buffer_4
  assign controlled_buffer_5_out = write ? In[4] : 1'bz;  // Controlled_Buffer controlled_buffer_5
  assign controlled_buffer_6_out = write ? In[5] : 1'bz;  // Controlled_Buffer controlled_buffer_6
  assign controlled_buffer_7_out = write ? In[6] : 1'bz;  // Controlled_Buffer controlled_buffer_7
  assign controlled_buffer_8_out = write ? In[7] : 1'bz;  // Controlled_Buffer controlled_buffer_8
  assign controlled_buffer_9_out = write ? In[8] : 1'bz;  // Controlled_Buffer controlled_buffer_9
  assign controlled_buffer_10_out = write ? In[9] : 1'bz;  // Controlled_Buffer controlled_buffer_10
  assign controlled_buffer_11_out = write ? In[10] : 1'bz;  // Controlled_Buffer controlled_buffer_11
  assign controlled_buffer_12_out = write ? In[11] : 1'bz;  // Controlled_Buffer controlled_buffer_12
  D_Flip_Flop d_ff_1 (.clk(CLK), .D(controlled_buffer_1_out), .Q(d_ff_1_q), .reset(Reset));  // open: Qn, preset, en
  D_Flip_Flop d_ff_2 (.clk(CLK), .D(controlled_buffer_2_out), .Q(d_ff_2_q), .reset(Reset));  // open: Qn, preset, en
  D_Flip_Flop d_ff_3 (.clk(CLK), .D(controlled_buffer_3_out), .Q(d_ff_3_q), .reset(Reset));  // open: Qn, preset, en
  D_Flip_Flop d_ff_4 (.clk(CLK), .D(controlled_buffer_4_out), .Q(d_ff_4_q), .reset(Reset));  // open: Qn, preset, en
  D_Flip_Flop d_ff_5 (.clk(CLK), .D(controlled_buffer_5_out), .Q(d_ff_5_q), .reset(Reset));  // open: Qn, preset, en
  D_Flip_Flop d_ff_6 (.clk(CLK), .D(controlled_buffer_6_out), .Q(d_ff_6_q), .reset(Reset));  // open: Qn, preset, en
  D_Flip_Flop d_ff_7 (.clk(CLK), .D(controlled_buffer_7_out), .Q(d_ff_7_q), .reset(Reset));  // open: Qn, preset, en
  D_Flip_Flop d_ff_8 (.clk(CLK), .D(controlled_buffer_8_out), .Q(d_ff_8_q), .reset(Reset));  // open: Qn, preset, en
  D_Flip_Flop d_ff_9 (.clk(CLK), .D(controlled_buffer_9_out), .Q(d_ff_9_q), .reset(Reset));  // open: Qn, preset, en
  D_Flip_Flop d_ff_10 (.clk(CLK), .D(controlled_buffer_10_out), .Q(d_ff_10_q), .reset(Reset));  // open: Qn, preset, en
  D_Flip_Flop d_ff_11 (.clk(CLK), .D(controlled_buffer_11_out), .Q(d_ff_11_q), .reset(Reset));  // open: Qn, preset, en
  D_Flip_Flop d_ff_12 (.clk(CLK), .D(controlled_buffer_12_out), .Q(d_ff_12_q), .reset(Reset));  // open: Qn, preset, en
  assign outY[0] = rA2 ? d_ff_1_q : 1'bz;  // Controlled_Buffer controlled_buffer_13
  assign outY[1] = rA2 ? d_ff_2_q : 1'bz;  // Controlled_Buffer controlled_buffer_14
  assign outX[0] = rA1 ? d_ff_1_q : 1'bz;  // Controlled_Buffer controlled_buffer_15
  assign outX[1] = rA1 ? d_ff_2_q : 1'bz;  // Controlled_Buffer controlled_buffer_16
  assign outX[2] = rA1 ? d_ff_3_q : 1'bz;  // Controlled_Buffer controlled_buffer_17
  assign outX[3] = rA1 ? d_ff_4_q : 1'bz;  // Controlled_Buffer controlled_buffer_18
  assign outY[2] = rA2 ? d_ff_3_q : 1'bz;  // Controlled_Buffer controlled_buffer_19
  assign outY[3] = rA2 ? d_ff_4_q : 1'bz;  // Controlled_Buffer controlled_buffer_20
  assign outY[4] = rA2 ? d_ff_5_q : 1'bz;  // Controlled_Buffer controlled_buffer_21
  assign outY[5] = rA2 ? d_ff_6_q : 1'bz;  // Controlled_Buffer controlled_buffer_22
  assign outX[4] = rA1 ? d_ff_5_q : 1'bz;  // Controlled_Buffer controlled_buffer_23
  assign outX[5] = rA1 ? d_ff_6_q : 1'bz;  // Controlled_Buffer controlled_buffer_24
  assign outX[6] = rA1 ? d_ff_7_q : 1'bz;  // Controlled_Buffer controlled_buffer_25
  assign outX[7] = rA1 ? d_ff_8_q : 1'bz;  // Controlled_Buffer controlled_buffer_26
  assign outY[6] = rA2 ? d_ff_7_q : 1'bz;  // Controlled_Buffer controlled_buffer_27
  assign outY[7] = rA2 ? d_ff_8_q : 1'bz;  // Controlled_Buffer controlled_buffer_28
  assign outY[8] = rA2 ? d_ff_9_q : 1'bz;  // Controlled_Buffer controlled_buffer_29
  assign outY[9] = rA2 ? d_ff_10_q : 1'bz;  // Controlled_Buffer controlled_buffer_30
  assign outX[8] = rA1 ? d_ff_9_q : 1'bz;  // Controlled_Buffer controlled_buffer_31
  assign outX[9] = rA1 ? d_ff_10_q : 1'bz;  // Controlled_Buffer controlled_buffer_32
  assign outX[10] = rA1 ? d_ff_11_q : 1'bz;  // Controlled_Buffer controlled_buffer_33
  assign outX[11] = rA1 ? d_ff_12_q : 1'bz;  // Controlled_Buffer controlled_buffer_34
  assign outY[10] = rA2 ? d_ff_11_q : 1'bz;  // Controlled_Buffer controlled_buffer_35
  assign outY[11] = rA2 ? d_ff_12_q : 1'bz;  // Controlled_Buffer controlled_buffer_36
endmodule

module U_control (
  input  [11:0] instruction,
  input  CLK,
  input  reset,
  input  [3:0] PC_in,
  output wA,
  output wB,
  output wC,
  output wD,
  output rA1,
  output rA2,
  output rB1,
  output rB2,
  output rC1,
  output rC2,
  output rD1,
  output rD2,
  output f0,
  output f1,
  output f2,
  output wAD,
  output [3:0] AD_out,
  output wPC,
  output Fetch,
  output [3:0] PC_out,
  output ext1,
  output ext2,
  output write,
  output read
);

  wire decoder_3_8_1_d4, decoder_3_8_1_d5, decoder_3_8_1_d6, decoder_3_8_1_d7, decoder_3_8_2_d0,
       decoder_3_8_2_d1, decoder_3_8_2_d2, decoder_3_8_2_d3;
  wire [3:0] full_adder_4bit_1_somme;
  wire [11:6] registre_12bit_1_outx;

  Decoder_3_8 decoder_3_8_1 (
    .e0(write), .e1(registre_12bit_1_outx[7]), .e2(registre_12bit_1_outx[6]), .D0(wA), .D1(wB), .D2(wC),
    .D3(wD), .D4(decoder_3_8_1_d4), .D5(decoder_3_8_1_d5), .D6(decoder_3_8_1_d6), .D7(decoder_3_8_1_d7));
  Registre_12bit registre_12bit_1 (
    .In(instruction), .write(1'b1), .outX({registre_12bit_1_outx, AD_out, ext2, ext1}), .CLK(CLK),
    .Reset(1'b0), .rA1(1'b1), .rA2(1'b0));  // open: outY
  or or_1 (rA1, decoder_3_8_1_d4, decoder_3_8_2_d0);
  Decoder_3_8 decoder_3_8_2 (
    .e0(wAD), .e1(AD_out[3]), .e2(AD_out[2]), .D0(decoder_3_8_2_d0), .D1(decoder_3_8_2_d1),
    .D2(decoder_3_8_2_d2), .D3(decoder_3_8_2_d3));  // open: D4, D5, D6, D7
  or or_2 (rB1, decoder_3_8_1_d5, decoder_3_8_2_d1);
  InsterDecodr insterdecodr_1 (
    .OpCod(registre_12bit_1_outx[11:8]), .f2(f2), .f1(f1), .f0(f0), .R(read), .W(write), .wAD(wAD),
    .wPC(wPC), .Fetch(Fetch));
  or or_3 (rC1, decoder_3_8_1_d6, decoder_3_8_2_d2);
  Decoder_3_8 decoder_3_8_3 (
    .e0(wAD), .e1(AD_out[1]), .e2(AD_out[0]), .D0(rA2), .D1(rB2), .D2(rC2), .D3(rD2));  // open: D4, D5, D6, D7
  or or_4 (rD1, decoder_3_8_1_d7, decoder_3_8_2_d3);
  MUX_1_4bits mux_1_4bits_1 (.OUT(PC_out), .in_0(4'b0000), .in_1(full_adder_4bit_1_somme), .sel(reset));
  Full_adder_4bit full_adder_4bit_1 (
    .number_1(PC_in), .number_2(4'b0001), .Somme(full_adder_4bit_1_somme));  // open: OverFlow
endmodule

// InstrDecoder
module InsterDecodr (
  input  [3:0] OpCod,
  output f2,
  output f1,
  output f0,
  output R,
  output W,
  output wAD,
  output wPC,
  output Fetch
);

  wire AND2_2_out, AND2_3_out, AND2_out, AND3_2_out, AND3_out, AND4_out, not_1_out, not_2_out, not_3_out,
       not_4_out, not_5_out, not_6_out, not_7_out, not_8_out, not_9_out, not_10_out, not_11_out, not_12_out,
       not_13_out, not_14_out, OR2_2_out, OR2_3_out, OR2_out, XOR2_out;

  not not_1 (not_1_out, OpCod[3]);
  not not_2 (not_2_out, OpCod[0]);
  not not_3 (not_3_out, OpCod[2]);
  not not_4 (not_4_out, OpCod[2]);
  not not_5 (not_5_out, OpCod[3]);
  not not_6 (not_6_out, OpCod[0]);
  not not_7 (not_7_out, OpCod[2]);
  not not_8 (not_8_out, OpCod[2]);
  not not_9 (not_9_out, OpCod[3]);
  not not_10 (not_10_out, OpCod[0]);
  not not_11 (not_11_out, OpCod[0]);
  not not_12 (not_12_out, OpCod[1]);
  not not_13 (not_13_out, OpCod[2]);
  not not_14 (not_14_out, OpCod[3]);
  or OR2 (OR2_out, OpCod[0], OpCod[1]);
  or OR2_2 (OR2_2_out, OpCod[0], not_4_out);
  and AND3 (AND3_out, OpCod[0], not_8_out, not_9_out);
  xor XOR2 (XOR2_out, OpCod[2], OpCod[3]);
  and AND2 (AND2_out, not_1_out, OpCod[2], OR2_out);
  and AND4 (AND4_out, not_2_out, OpCod[1], not_3_out, OpCod[3]);
  and AND2_2 (AND2_2_out, OR2_2_out, not_5_out);
  or OR2_3 (OR2_3_out, AND2_2_out, AND2_3_out);
  and AND2_3 (AND2_3_out, not_6_out, not_7_out, OpCod[3]);
  and AND3_2 (AND3_2_out, not_10_out, OpCod[1], XOR2_out);
  and AND4_2 (R, not_11_out, not_12_out, OpCod[2], not_14_out);
  and AND4_3 (W, not_11_out, not_12_out, not_13_out, OpCod[3]);
  or OR2_4 (f2, AND2_out, AND4_out);
  and AND2_4 (f1, OpCod[1], OR2_3_out);
  or OR2_5 (f0, AND3_out, AND3_2_out);
  or OR2_6 (wAD, R, W);

  assign Fetch = 1'b1;
  assign wPC = 1'b1;
endmodule

module MUX_2_4 (
  input  [3:0] in_0,
  input  [3:0] in_1,
  input  sel,
  output [3:0] OUT
);

  MUX_1_2 mux_1_2_1 (.e0(in_1[0]), .e1(in_0[0]), .Sel(sel), .out_4(OUT[0]));
  MUX_1_2 mux_1_2_2 (.e0(in_1[1]), .e1(in_0[1]), .Sel(sel), .out_4(OUT[1]));
  MUX_1_2 mux_1_2_3 (.e0(in_1[2]), .e1(in_0[2]), .Sel(sel), .out_4(OUT[2]));
  MUX_1_2 mux_1_2_4 (.e0(in_1[3]), .e1(in_0[3]), .Sel(sel), .out_4(OUT[3]));
endmodule
